# Fritzing sketch Untitled Sketch 2 (saved by Fritzing 0.9.3b)

parts:
  Part1 = Arduino Nano (Rev3.0)
  Part2 = Bluetooth HC-05 Macho
  S1 = H-Bridge with L298N
  U1 = LCD-16X2 [package=lcd-16x2_noholes]  # not connected
  M1 = DC Motor
  M2 = DC Motor
  VCC1 = Battery

nets:
  N1: Part1.D2, Part2.TXD
  N2: Part1.D3, Part2.RXD
  N3: Part1.D7, S1.IN4
  N4: Part1.D8, S1.IN3
  N5: Part1.D9, S1.IN2
  N6: Part1.D10, S1.IN1
  N7: Part1.D11/MOSI, S1.ENB
  N8: Part1.D12/MISO, S1.ENA
  VIN: Part1.VIN, S1.5V
  GND: Part1.GND, Part2.GND, S1.GND, VCC1.-
  5V: Part1.5V, Part2.VCC
  N9: S1.12V, VCC1.+
  N10: S1.M1-01, M2.pin_2
  N11: S1.M1-02, M2.pin_1
  N12: S1.M2-01, M1.pin_2
  N13: S1.M2-02, M1.pin_1

notes:
  i2c conections to 16x2 LCD

custom parts:
  H-Bridge with L298N: h-bridge
